# Fritzing sketch Bollerwagen.500 (saved by Fritzing 0.9.4)

parts:
  Arduino = Arduino Nano (Rev3.0)
  V1 = DC Power [voltage=12V]  # not connected
  npn = NPN-Transistor [package="SOT-23 [SMD]"]
  R1 = Resistor [tolerance=±5% resistance=10k package=THT]
  Roter_Pushbutton = Pushbutton [package=THT]
  3_Pol_Stecker = JST-B3P-VH [package=THT]
  3_Pol_Stecker_2 = JST-VHR-3N [part_number=JST-VHR-3N package=THT]
  LED_Strip = ws2812b [package="smd 2812b"]
  V2 = DC Power [voltage=5V]
  V3 = DC Power [voltage=5V]

nets:
  N1: Arduino.GND, R1.Pin_0, 3_Pol_Stecker.pin1, V2.V-
  N2: Arduino.D2, npn.0
  N3: Arduino.D3, Roter_Pushbutton.leg1
  N4: Arduino.D5, 3_Pol_Stecker.pin2
  N5: Arduino.VIN, V3.V+
  N6: Arduino.5V, Roter_Pushbutton.leg0
  N7: npn.2, R1.Pin_1
  N8: 3_Pol_Stecker.pin3, V2.V+
  N9: 3_Pol_Stecker_2.pin_5, LED_Strip.DIN
  N10: 3_Pol_Stecker_2.pin_4, LED_Strip.VSS
  N11: 3_Pol_Stecker_2.pin_6, LED_Strip.VDD
